# Fritzing sketch m365 (saved by Fritzing 0.9.3b)
circuit board: 6.86839cm x 2.66361cm
circuit board: 6.86839cm x 2.66361cm

parts:
  OLED_0'91_I2c = Grove OLED 128x96
  R1 = Resistor [tolerance=±5% resistance=1k package=THT]
  R2 = Resistor [tolerance=±5% resistance=1k package=THT]
  R3 = Resistor [tolerance=±5% resistance=1k package=THT]
  R4 = Resistor [tolerance=±5% resistance=1k package=THT]
  R5 = Resistor [tolerance=±5% resistance=10k package=THT]
  R6 = Resistor [tolerance=±5% resistance=10k package=THT]
  R7 = Resistor [tolerance=±5% resistance=10k package=THT]
  R8 = Resistor [tolerance=±5% resistance=10k package=THT]
  R9 = Resistor [tolerance=±5% resistance=10k package=THT]
  R10 = Resistor [tolerance=±5% resistance=10k package=THT]
  R11 = Resistor [tolerance=±5% resistance=10k package=THT]
  R12 = Resistor [tolerance=±5% resistance=10k package=THT]
  R14 = Resistor [tolerance=±5% resistance=1k package=THT]
  R15 = Resistor [tolerance=±5% resistance=1k package=THT]
  R16 = Resistor [tolerance=±5% resistance=1k package=THT]
  BTN_1 = Pushbutton [package="[THT]"]
  BTN_2 = Pushbutton [package="[THT]"]
  BTN_3 = Pushbutton [package="[THT]"]
  BTN_4 = Pushbutton [package="[THT]"]
  BTN_5 = Pushbutton [package="[THT]"]
  BTN_6 = Pushbutton [package="[THT]"]
  BTN_7 = Pushbutton [package="[THT]"]
  BTN_8 = Pushbutton [package="[THT]"]
  MCU1 = Raspberry Pi Zero
  R13 = Resistor [tolerance=±5% resistance=1k package=THT]

nets:
  N1: OLED_0'91_I2c.GND, R5.Pin_1, R6.Pin_1, R7.Pin_1, R8.Pin_1, R9.Pin_1, R10.Pin_1, R11.Pin_1, R12.Pin_1, MCU1.pin_6, MCU1.pin_9, MCU1.pin_34, MCU1.pin_39
  N2: OLED_0'91_I2c.VCC, BTN_1.Pin_3, BTN_1.Pin_4, BTN_2.Pin_3, BTN_2.Pin_4, BTN_3.Pin_3, BTN_3.Pin_4, BTN_4.Pin_3, BTN_5.Pin_3, BTN_5.Pin_4, BTN_6.Pin_3, BTN_6.Pin_4, BTN_7.Pin_3, BTN_7.Pin_4, BTN_8.Pin_4, MCU1.pin_1, MCU1.pin_17
  N3: OLED_0'91_I2c.SDA, MCU1.pin_3
  N4: OLED_0'91_I2c.SCL, MCU1.pin_5
  N5: R1.Pin_0, R8.Pin_0, BTN_1.Pin_1, BTN_1.Pin_2
  N6: R1.Pin_1, MCU1.pin_31
  N7: R2.Pin_0, R7.Pin_0, BTN_2.Pin_1, BTN_2.Pin_2
  N8: R2.Pin_1, MCU1.pin_33
  N9: R3.Pin_0, R6.Pin_0, BTN_3.Pin_1, BTN_3.Pin_2
  N10: R3.Pin_1, MCU1.pin_35
  N11: R4.Pin_0, R5.Pin_0, BTN_4.Pin_1, BTN_4.Pin_2
  N12: R4.Pin_1, MCU1.pin_37
  N13: R9.Pin_0, R15.Pin_0, BTN_7.Pin_1, BTN_7.Pin_2
  N14: R10.Pin_0, R14.Pin_0, BTN_6.Pin_1, BTN_6.Pin_2
  N15: R11.Pin_0, R16.Pin_0, BTN_8.Pin_1, BTN_8.Pin_2
  N16: R12.Pin_0, BTN_5.Pin_1, BTN_5.Pin_2, R13.Pin_0
  N17: R14.Pin_1, MCU1.pin_36
  N18: R15.Pin_1, MCU1.pin_38
  N19: R16.Pin_1, MCU1.pin_40
  N20: MCU1.pin_32, R13.Pin_1
